# Fritzing sketch Montagem - Sinaleiro e Ponte (saved by Fritzing 0.9.3b)

parts:
  Componente1 = Arduino Uno (Rev3)
  LED1 = LED - 5mm [color="Green (570nm)" package="5 mm [THT]"]
  LED2 = LED - 5mm [color="Red (633nm)" package="5 mm [THT]"]
  LED3 = LED - 5mm [color="Yellow (595nm)" package="5 mm [THT]"]
  R1 = Resistor [tolerance=±20% resistance=1k package=THT]
  J1 = Basic Servo

nets:
  N1: Componente1.D11_PWM/MOSI, LED1.anode
  N2: Componente1.D12/MISO, LED3.anode
  N3: Componente1.D13/SCK, LED2.anode
  GND: Componente1.GND, R1.Pin_0, J1.gnd
  N4: Componente1.D4, J1.pulse
  5V: Componente1.5V, J1.vcc
  N5: LED1.cathode, LED2.cathode, LED3.cathode, R1.Pin_1
